# Fritzing sketch circuit_diagram (saved by Fritzing 0.9.9b)
breadboards: 1

parts:
  Raspberry_Pi1 = Raspberry Pi 2
  S1 = Momentary Switch [package=ksa_sealed_tac_switch]
  S2 = Momentary Switch [package=ksa_sealed_tac_switch]
  S3 = Momentary Switch [package=ksa_sealed_tac_switch]
  LED1 = smd LED [color="Red (633nm)" package="0603 [SMD]"]
  LED2 = smd LED [color="Green (560nm)" package="0603 [SMD]"]
  LED3 = smd LED [color="Blue (430nm)" package="0603 [SMD]"]
  R1 = Resistor [tolerance=±5% resistance=10000 package="0805 [SMD]"]
  R2 = Resistor [tolerance=±5% resistance=1000 package="0805 [SMD]"]
  R3 = Resistor [tolerance=±5% resistance=10000 package="0805 [SMD]"]

nets:
  N1: Raspberry_Pi1.GPIO4, S2.3, S2.4
  N2: Raspberry_Pi1.GPIO17, S1.3, S1.4
  N3: Raspberry_Pi1.GPIO27, S3.3, S3.4
  N4: Raspberry_Pi1.GND, R1.Pin_0, R2.Pin_0, R3.Pin_0
  N5: Raspberry_Pi1.GPIO16, LED2.cathode
  N6: Raspberry_Pi1.GPIO12, LED1.cathode
  N7: Raspberry_Pi1.GPIO18, LED3.cathode
  N8: S1.1, S1.2, S2.1, S2.2, S3.1, S3.2
  N9: LED1.anode, R1.Pin_1
  N10: LED2.anode, R2.Pin_1
  N11: LED3.anode, R3.Pin_1
